// Logisim project simulator.circ as structural Verilog: 10 circuits, main circuit main
module main (
);

  wire clk, control_unit_1_isbeq, control_unit_1_isbgt, control_unit_1_isimmediate, control_unit_1_isret,
       control_unit_1_isubranch, ex_unit_1_is_branch_taken, I_bit, is_Ld, Is_St, isCall, wb;
  wire [3:0] rd, reg_src;
  wire [4:0] opcode;
  wire [12:0] control_unit_1_alusignals;
  wire [31:0] ex_unit_1_alu_result, if_unit_1_instruction, if_unit_1_pc, ma_unit_1_ldresult,
       of_unit_1_branchtarget, of_unit_1_immx, of_unit_1_op1, of_unit_1_op2, reg_val;

  IF_unit if_unit_1 (
    .Clock(clk), .isBranchTaken(ex_unit_1_is_branch_taken), .Branch_Target(of_unit_1_branchtarget),
    .PC(if_unit_1_pc), .Instruction(if_unit_1_instruction));
  Control_Unit control_unit_1 (
    .I_bit(I_bit), .opcode(opcode), .isSt(Is_St), .isLd(is_Ld), .isBeq(control_unit_1_isbeq),
    .isBgt(control_unit_1_isbgt), .isRet(control_unit_1_isret), .isImmediate(control_unit_1_isimmediate),
    .isWb(wb), .isUbranch(control_unit_1_isubranch), .isCall(isCall), .ALUsignals(control_unit_1_alusignals));
  Clock clock_1 (.out(clk));
  OF_unit of_unit_1 (
    .PC(if_unit_1_pc), .Instruction(if_unit_1_instruction), .Register_Clock(clk),
    .branchTarget(of_unit_1_branchtarget), .immx(of_unit_1_immx), .op1(of_unit_1_op1),
    .isRet(control_unit_1_isret), .op2(of_unit_1_op2), .Enable_Write(wb), .Write_Address(reg_src),
    .Value_To_Write(reg_val), .isSt(Is_St), .Opcode(opcode), .I_bit(I_bit), .rd(rd));
  EX_unit ex_unit_1 (
    .Is_uBranch(control_unit_1_isubranch), .isBgt(control_unit_1_isbgt), .isBeq(control_unit_1_isbeq),
    .clock(clk), .op1(of_unit_1_op1), .op2(of_unit_1_op2), .immx(of_unit_1_immx),
    .Is_Branch_Taken(ex_unit_1_is_branch_taken), .AlU_result(ex_unit_1_alu_result),
    .ALUsignals(control_unit_1_alusignals), .is_immx(control_unit_1_isimmediate));  // open: flag_GT, flag_E
  MA_unit ma_unit_1 (
    .MDR(of_unit_1_op2), .MAR(ex_unit_1_alu_result), .ldResult(ma_unit_1_ldresult), .isSt(Is_St),
    .isLd(is_Ld), .clk(clk));
  RW_unit rw_unit_1 (
    .Write_Address(reg_src), .aluResult(ex_unit_1_alu_result), .ldResult(ma_unit_1_ldresult),
    .pc(if_unit_1_pc), .isLd(is_Ld), .isCall(isCall), .rd(rd), .Data_To_Write(reg_val));
endmodule

module register_file (
  input  [31:0] Value_to_Write,
  input  [3:0] Write_Port_IP,
  input  Clock_for_registers,
  input  [3:0] Read_Port_IP_1,
  input  [3:0] Read_Port_IP_2,
  input  Enable_Write,
  output [31:0] Read_Port_OP_1,
  output [31:0] Read_Port_OP_2
);

  wire decoder_1_out0, decoder_1_out1, decoder_1_out2, decoder_1_out3, decoder_1_out4, decoder_1_out5,
       decoder_1_out6, decoder_1_out7, decoder_1_out8, decoder_1_out9, decoder_1_out10, decoder_1_out11,
       decoder_1_out12, decoder_1_out13, decoder_1_out14, decoder_1_out15;
  wire [31:0] demultiplexer_1_out0, demultiplexer_1_out1, demultiplexer_1_out2, demultiplexer_1_out3,
       demultiplexer_1_out4, demultiplexer_1_out5, demultiplexer_1_out6, demultiplexer_1_out7,
       demultiplexer_1_out8, demultiplexer_1_out9, demultiplexer_1_out10, demultiplexer_1_out11,
       demultiplexer_1_out12, demultiplexer_1_out13, demultiplexer_1_out14, demultiplexer_1_out15, r0_q,
       r1_q, r2_q, r3_q, r4_q, r5_q, r6_q, r7_q, r8_q, r9_q, r10_q, r11_q, r12_q, r13_q, r14_q, r15_q;

  Register #(.width(32), .trigger("falling")) r0 (
    .D(demultiplexer_1_out0), .en(decoder_1_out0), .Q(r0_q), .clk(Clock_for_registers));  // open: clr
  Register #(.width(32), .trigger("falling")) r1 (
    .D(demultiplexer_1_out1), .en(decoder_1_out1), .Q(r1_q), .clk(Clock_for_registers));  // open: clr
  Register #(.width(32), .trigger("falling")) r2 (
    .D(demultiplexer_1_out2), .en(decoder_1_out2), .Q(r2_q), .clk(Clock_for_registers));  // open: clr
  Register #(.width(32), .trigger("falling")) r3 (
    .D(demultiplexer_1_out3), .en(decoder_1_out3), .Q(r3_q), .clk(Clock_for_registers));  // open: clr
  Multiplexer #(.select(4), .width(32), .enable("false")) multiplexer_1 (
    .in0(r0_q), .in1(r1_q), .in2(r2_q), .in3(r3_q), .in4(r4_q), .in5(r5_q), .in6(r6_q), .in7(r7_q),
    .in8(r8_q), .in9(r9_q), .in10(r10_q), .in11(r11_q), .in12(r12_q), .in13(r13_q), .in14(r14_q),
    .in15(r15_q), .out(Read_Port_OP_1), .sel(Read_Port_IP_1));
  Demultiplexer #(.select(4), .width(32), .enable("false")) demultiplexer_1 (
    .out0(demultiplexer_1_out0), .out1(demultiplexer_1_out1), .out2(demultiplexer_1_out2),
    .out3(demultiplexer_1_out3), .out4(demultiplexer_1_out4), .out5(demultiplexer_1_out5),
    .out6(demultiplexer_1_out6), .out7(demultiplexer_1_out7), .out8(demultiplexer_1_out8),
    .out9(demultiplexer_1_out9), .out10(demultiplexer_1_out10), .out11(demultiplexer_1_out11),
    .out12(demultiplexer_1_out12), .out13(demultiplexer_1_out13), .out14(demultiplexer_1_out14),
    .out15(demultiplexer_1_out15), .in(Value_to_Write), .sel(Write_Port_IP));
  Register #(.width(32), .trigger("falling")) r4 (
    .D(demultiplexer_1_out4), .en(decoder_1_out4), .Q(r4_q), .clk(Clock_for_registers));  // open: clr
  Register #(.width(32), .trigger("falling")) r5 (
    .D(demultiplexer_1_out5), .en(decoder_1_out5), .Q(r5_q), .clk(Clock_for_registers));  // open: clr
  Register #(.width(32), .trigger("falling")) r6 (
    .D(demultiplexer_1_out6), .en(decoder_1_out6), .Q(r6_q), .clk(Clock_for_registers));  // open: clr
  Register #(.width(32), .trigger("falling")) r7 (
    .D(demultiplexer_1_out7), .en(decoder_1_out7), .Q(r7_q), .clk(Clock_for_registers));  // open: clr
  Multiplexer #(.select(4), .width(32), .enable("false")) multiplexer_2 (
    .in0(r0_q), .in1(r1_q), .in2(r2_q), .in3(r3_q), .in4(r4_q), .in5(r5_q), .in6(r6_q), .in7(r7_q),
    .in8(r8_q), .in9(r9_q), .in10(r10_q), .in11(r11_q), .in12(r12_q), .in13(r13_q), .in14(r14_q),
    .in15(r15_q), .out(Read_Port_OP_2), .sel(Read_Port_IP_2));
  Register #(.width(32), .trigger("falling")) r8 (
    .D(demultiplexer_1_out8), .en(decoder_1_out8), .Q(r8_q), .clk(Clock_for_registers));  // open: clr
  Register #(.width(32), .trigger("falling")) r9 (
    .D(demultiplexer_1_out9), .en(decoder_1_out9), .Q(r9_q), .clk(Clock_for_registers));  // open: clr
  Register #(.width(32), .trigger("falling")) r11 (
    .D(demultiplexer_1_out11), .en(decoder_1_out11), .Q(r11_q), .clk(Clock_for_registers));  // open: clr
  Register #(.width(32), .trigger("falling")) r10 (
    .D(demultiplexer_1_out10), .en(decoder_1_out10), .Q(r10_q), .clk(Clock_for_registers));  // open: clr
  Register #(.width(32), .trigger("falling")) r12 (
    .D(demultiplexer_1_out12), .en(decoder_1_out12), .Q(r12_q), .clk(Clock_for_registers));  // open: clr
  Decoder #(.select(4), .disabled(0)) decoder_1 (
    .out0(decoder_1_out0), .out1(decoder_1_out1), .out2(decoder_1_out2), .out3(decoder_1_out3),
    .out4(decoder_1_out4), .out5(decoder_1_out5), .out6(decoder_1_out6), .out7(decoder_1_out7),
    .out8(decoder_1_out8), .out9(decoder_1_out9), .out10(decoder_1_out10), .out11(decoder_1_out11),
    .out12(decoder_1_out12), .out13(decoder_1_out13), .out14(decoder_1_out14), .out15(decoder_1_out15),
    .sel(Write_Port_IP), .en(Enable_Write));
  Register #(.width(32), .trigger("falling")) r13 (
    .D(demultiplexer_1_out13), .en(decoder_1_out13), .Q(r13_q), .clk(Clock_for_registers));  // open: clr
  Register #(.width(32), .trigger("falling")) r14 (
    .D(demultiplexer_1_out14), .en(decoder_1_out14), .Q(r14_q), .clk(Clock_for_registers));  // open: clr
  Register #(.width(32), .trigger("falling")) r15 (
    .D(demultiplexer_1_out15), .en(decoder_1_out15), .Q(r15_q), .clk(Clock_for_registers));  // open: clr
endmodule

module IF_unit (
  input  isBranchTaken,
  input  [31:0] Branch_Target,
  input  Clock,
  output [31:0] PC,
  output [31:0] Instruction
);

  wire [23:0] bit_extender_1_out;
  wire [31:0] adder_1_out, multiplexer_1_out;

  Register #(.width(32), .trigger("falling")) u_PC (
    .D(multiplexer_1_out), .en(1'b1), .Q(PC), .clk(Clock));  // open: clr
  Bit_Extender #(.in_width(32), .out_width(24)) bit_extender_1 (.in(PC), .out(bit_extender_1_out));
  Multiplexer #(.width(32), .enable("false")) multiplexer_1 (
    .in0(adder_1_out), .in1(Branch_Target), .out(multiplexer_1_out), .sel(isBranchTaken));
  Adder #(.width(32)) adder_1 (.a(32'h1), .b(PC), .out(adder_1_out));  // open: cin, cout
  ROM #(.addrWidth(24), .dataWidth(32)) rom_1 (.addr(bit_extender_1_out), .data(Instruction), .sel(1'b1));

  // Notes on the sheet:
  //   contents of rom_1 (hex, n*v repeats v):
  //   4c000004 4cc00001 4f801000 98000003 7c4c0000 90000000 280c0000 8000000c 8800000b fb80008 7c380000
  //   7ff80004 c000001 9ffffff9 74380000 77f80004 10404000 7b80008 a0000000 4c400001 a0000000
endmodule

module OF_unit (
  input  [31:0] PC,
  input  isRet,
  input  [31:0] Instruction,
  input  Enable_Write,
  input  [3:0] Write_Address,
  input  [31:0] Value_To_Write,
  input  isSt,
  input  Register_Clock,
  output [31:0] branchTarget,
  output [31:0] immx,
  output [31:0] op1,
  output [31:0] op2,
  output [3:0] rd,
  output I_bit,
  output [4:0] Opcode
);

  wire [3:0] multiplexer_1_out, multiplexer_2_out;
  wire [31:0] adder_1_out, bit_extender_1_out;

  calculate_immx calculate_immx_1 (.op_immx(Instruction[17:0]), .immediate(immx));
  assign bit_extender_1_out = {{5{Instruction[26]}}, Instruction[26:0]};  // Bit_Extender bit_extender_1
  Multiplexer #(.width(4), .enable("false")) multiplexer_1 (
    .in0(Instruction[21:18]), .in1(4'b1111), .out(multiplexer_1_out), .sel(isRet));
  Multiplexer #(.width(4), .enable("false")) multiplexer_2 (
    .in0(Instruction[17:14]), .in1(Instruction[25:22]), .out(multiplexer_2_out), .sel(isSt));
  Adder #(.width(32)) adder_1 (.a(PC), .b(bit_extender_1_out), .out(adder_1_out));  // open: cin, cout
  register_file Register_File (
    .Clock_for_registers(Register_Clock), .Enable_Write(Enable_Write), .Value_to_Write(Value_To_Write),
    .Write_Port_IP(Write_Address), .Read_Port_IP_1(multiplexer_1_out), .Read_Port_OP_1(op1),
    .Read_Port_IP_2(multiplexer_2_out), .Read_Port_OP_2(op2));
  Multiplexer #(.width(32), .enable("false")) multiplexer_3 (
    .in0(adder_1_out), .in1(op1), .out(branchTarget), .sel(isRet));

  assign I_bit = Instruction[26];
  assign Opcode = Instruction[31:27];
  assign rd = Instruction[25:22];

  // Notes on the sheet:
  //   Calculates Immediate
endmodule

module calculate_immx (
  input  [17:0] op_immx,
  output [31:0] immediate
);

  wire [31:0] bit_extender_1_out, bit_extender_2_out, shifter_1_out;

  assign bit_extender_1_out = {{16{op_immx[15]}}, op_immx[15:0]};  // Bit_Extender bit_extender_1
  assign bit_extender_2_out = {{16{1'b0}}, op_immx[15:0]};  // Bit_Extender bit_extender_2
  Shifter #(.width(32)) shifter_1 (.in(bit_extender_2_out), .\dist (5'b10000), .out(shifter_1_out));
  Multiplexer #(.select(2), .width(32), .enable("false")) multiplexer_1 (
    .in0(bit_extender_1_out), .in1(bit_extender_2_out), .in2(shifter_1_out), .out(immediate),
    .sel(op_immx[17:16]));  // open: in3
endmodule

module RW_unit (
  input  [3:0] rd,
  input  [31:0] aluResult,
  input  [31:0] ldResult,
  input  [31:0] pc,
  input  isLd,
  input  isCall,
  output [3:0] Write_Address,
  output [31:0] Data_To_Write
);

  wire [31:0] adder_1_out;

  Adder #(.width(32)) adder_1 (.a(pc), .b(32'h1), .out(adder_1_out));  // open: cin, cout
  Multiplexer #(.select(2), .width(32), .enable("false")) multiplexer_1 (
    .in0(aluResult), .in1(ldResult), .in2(adder_1_out), .out(Data_To_Write), .sel({isCall, isLd}));  // open: in3
  Multiplexer #(.width(4), .enable("false")) multiplexer_2 (.in0(rd), .in1(4'b1111), .out(Write_Address), .sel(isCall));
endmodule

module MA_unit (
  input  [31:0] MDR,
  input  clk,
  input  [31:0] MAR,
  input  isSt,
  input  isLd,
  output [31:0] ldResult
);

  wire or_1_out;

  assign ldResult = isSt ? MDR : 32'bz;  // Controlled_Buffer controlled_buffer_1
  or or_1 (or_1_out, isSt, isLd);
  RAM #(.addrWidth(24), .dataWidth(32)) ram_1 (
    .addr(MAR[23:0]), .data(ldResult), .sel(or_1_out), .clk(clk), .ld(isLd));  // open: clr
endmodule

module alu (
  input  [31:0] A,
  input  [31:0] B,
  input  [12:0] ALUsignals,
  output GT_flag,
  output E_flag,
  output [31:0] Aluresult
);

  wire comparator_1_eq, not_4_out, not_9_out, transmission_1_p1, transmission_1_p3;
  wire [31:0] adder_1_out, and_1_out, divider_1_out, divider_1_rem, multiplier_1_out, not_8_out, or_1_out,
       shifter_1_out, shifter_2_out, shifter_3_out, subtractor_1_out;

  // Transmission_Gate transmission_1: pin names not known; wires that end beside it: transmission_1_p1, GT_flag, transmission_1_p3, ALUsignals[0]
  Comparator #(.width(32)) comparator_1 (.a(A), .b(B), .gt(transmission_1_p3), .eq(comparator_1_eq));  // open: lt
  Adder #(.width(32)) adder_1 (.a(A), .b(B), .out(adder_1_out));  // open: cin, cout
  Subtractor #(.width(32)) subtractor_1 (.a(A), .b(B), .out(subtractor_1_out));  // open: bin, bout
  Multiplier #(.width(32)) multiplier_1 (.a(A), .b(B), .out(multiplier_1_out));  // open: cin, cout
  Divider #(.width(32)) divider_1 (.a(A), .b(B), .out(divider_1_out), .rem(divider_1_rem));  // open: upper
  Shifter #(.width(32)) shifter_1 (.in(A), .\dist (B[4:0]), .out(shifter_1_out));
  Shifter #(.width(32), .shift("lr")) shifter_2 (.in(A), .\dist (B[4:0]), .out(shifter_2_out));
  Shifter #(.width(32), .shift("ar")) shifter_3 (.in(A), .\dist (B[4:0]), .out(shifter_3_out));
  // NOT_Gate not_1 has open pins: in=ALUsignals[9], out=open
  not not_2 (transmission_1_p1, ALUsignals[0]);
  // NOT_Gate not_3 has open pins: in=ALUsignals[4], out=open
  // Transmission_Gate #(.width(32)) transmission_2: pin names not known; wires that end beside it: divider_1_out, ALUsignals[4], Aluresult
  // Transmission_Gate #(.width(32)) transmission_3: pin names not known; wires that end beside it: shifter_3_out, Aluresult
  not not_4 (not_4_out, ALUsignals[0]);
  // Transmission_Gate transmission_4: pin names not known; wires that end beside it: not_4_out, E_flag, comparator_1_eq, ALUsignals[0]
  // NOT_Gate not_5 has open pins: in=ALUsignals[5], out=open
  // Transmission_Gate #(.width(32)) transmission_5: pin names not known; wires that end beside it: divider_1_rem, ALUsignals[5], Aluresult
  // NOT_Gate not_6 has open pins: in=ALUsignals[8], out=open
  // Transmission_Gate #(.width(32)) transmission_6: pin names not known; wires that end beside it: shifter_2_out, ALUsignals[8], Aluresult
  // NOT_Gate not_7 has open pins: in=ALUsignals[7], out=open
  // Transmission_Gate #(.width(32)) transmission_7: pin names not known; wires that end beside it: shifter_1_out, ALUsignals[7]
  assign not_8_out = ~A;  // NOT_Gate not_8, 32 bits wide
  assign or_1_out = A | B;  // OR_Gate or_1, 32 bits wide
  assign and_1_out = A & B;  // AND_Gate and_1, 32 bits wide
  not not_9 (not_9_out, ALUsignals[1]);
  // Transmission_Gate #(.width(32)) transmission_8: pin names not known; wires that end beside it: adder_1_out, not_9_out, ALUsignals[1], Aluresult
  // NOT_Gate not_10 has open pins: in=ALUsignals[2], out=open
  // NOT_Gate not_11 has open pins: in=ALUsignals[11], out=open
  // Transmission_Gate #(.width(32)) transmission_9: pin names not known; wires that end beside it: and_1_out, ALUsignals[11], Aluresult
  // Transmission_Gate #(.width(32)) transmission_10: pin names not known; wires that end beside it: subtractor_1_out, ALUsignals[2], Aluresult
  // NOT_Gate not_12 has open pins: in=ALUsignals[3], out=open
  // Transmission_Gate #(.width(32)) transmission_11: pin names not known; wires that end beside it: multiplier_1_out, ALUsignals[3], Aluresult
  // NOT_Gate not_13 has open pins: in=ALUsignals[12], out=open
  // NOT_Gate not_14 has open pins: in=ALUsignals[10], out=open
  // Transmission_Gate #(.width(32)) transmission_12: pin names not known; wires that end beside it: not_8_out, ALUsignals[10]
  // Transmission_Gate #(.width(32)) transmission_13: pin names not known; wires that end beside it: or_1_out, ALUsignals[12], Aluresult
  // NOT_Gate not_15 has open pins: in=ALUsignals[6], out=open
  // Transmission_Gate #(.width(32)) transmission_14: pin names not known; wires that end beside it: Aluresult, ALUsignals[6], B

  // Other names for the same wires on the sheet: a_t[4:0] = {ALUsignals[9:7], ALUsignals[5:4]}
endmodule

module Control_Unit (
  input  I_bit,
  input  [4:0] opcode,
  output isSt,
  output isLd,
  output isBeq,
  output isBgt,
  output isRet,
  output isImmediate,
  output isWb,
  output isUbranch,
  output isCall,
  output [12:0] ALUsignals
);

  wire and_6_out, and_7_out, and_8_out, and_9_out, and_10_out, and_12_out, and_13_out, nand_1_out;

  nand nand_1 (nand_1_out, opcode[0], opcode[1]);
  and and_1 (isSt, opcode[0], opcode[1], opcode[2], opcode[3], ~opcode[4]);  // AND_Gate
  and and_2 (isLd, ~opcode[0], opcode[1], opcode[2], opcode[3], ~opcode[4]);  // AND_Gate
  and and_3 (isBeq, ~opcode[0], ~opcode[1], ~opcode[2], ~opcode[3], opcode[4]);  // AND_Gate
  and and_4 (isBgt, opcode[0], ~opcode[1], ~opcode[2], ~opcode[3], opcode[4]);  // AND_Gate
  and and_5 (isRet, ~opcode[0], ~opcode[1], opcode[2], ~opcode[3], opcode[4]);  // AND_Gate
  and and_6 (and_6_out, opcode[0], ~opcode[1], opcode[2], ~opcode[4]);  // AND_Gate
  and and_7 (and_7_out, opcode[0], opcode[2], opcode[3], ~opcode[4]);  // AND_Gate
  and and_8 (and_8_out, opcode[4], nand_1_out);
  and and_9 (and_9_out, opcode[1], ~opcode[2], ~opcode[3], opcode[4]);  // AND_Gate
  and and_10 (and_10_out, ~opcode[0], ~opcode[1], opcode[2], ~opcode[3], opcode[4]);  // AND_Gate
  and and_11 (isCall, opcode[0], opcode[1], ~opcode[2], ~opcode[3], opcode[4]);  // AND_Gate
  and and_12 (and_12_out, ~opcode[0], ~opcode[1], ~opcode[2], ~opcode[3], ~opcode[4]);  // AND_Gate
  and and_13 (and_13_out, opcode[1], opcode[2], opcode[3], ~opcode[4]);  // AND_Gate
  and isSub (ALUsignals[2], opcode[0], ~opcode[1], ~opcode[2], ~opcode[3], ~opcode[4]);  // AND_Gate
  and isCmp (ALUsignals[0], opcode[0], ~opcode[1], opcode[2], ~opcode[3], ~opcode[4]);  // AND_Gate
  and isMul (ALUsignals[3], ~opcode[0], opcode[1], ~opcode[2], ~opcode[3], ~opcode[4]);  // AND_Gate
  and isDiv (ALUsignals[4], opcode[0], opcode[1], ~opcode[2], ~opcode[3], ~opcode[4]);  // AND_Gate
  and isMod (ALUsignals[5], ~opcode[0], ~opcode[1], opcode[2], ~opcode[3], ~opcode[4]);  // AND_Gate
  and isLsl (ALUsignals[7], ~opcode[0], opcode[1], ~opcode[2], opcode[3], ~opcode[4]);  // AND_Gate
  and isLsr (ALUsignals[8], opcode[0], opcode[1], ~opcode[2], opcode[3], ~opcode[4]);  // AND_Gate
  and isAsr (ALUsignals[9], ~opcode[0], ~opcode[1], opcode[2], opcode[3], ~opcode[4]);  // AND_Gate
  and isOr (ALUsignals[12], opcode[0], opcode[1], opcode[2], ~opcode[3], ~opcode[4]);  // AND_Gate
  and isAnd (ALUsignals[11], ~opcode[0], opcode[1], opcode[2], ~opcode[3], ~opcode[4]);  // AND_Gate
  and isNot (ALUsignals[10], ~opcode[0], ~opcode[1], ~opcode[2], opcode[3], ~opcode[4]);  // AND_Gate
  and isMov (ALUsignals[6], opcode[0], ~opcode[1], ~opcode[2], opcode[3], ~opcode[4]);  // AND_Gate
  nor nor_1 (isWb, and_6_out, and_7_out, and_8_out);
  or or_1 (isUbranch, and_9_out, and_10_out);
  or isAdd (ALUsignals[1], and_12_out, and_13_out);

  assign isImmediate = I_bit;

  // Notes on the sheet:
  //   op1
  //   op2
  //   op3
  //   op4
  //   op5
endmodule

module EX_unit (
  input  Is_uBranch,
  input  isBgt,
  input  isBeq,
  input  clock,
  input  [31:0] op1,
  input  [31:0] op2,
  input  [12:0] ALUsignals,
  input  [31:0] immx,
  input  is_immx,
  output Is_Branch_Taken,
  output flag_GT,
  output flag_E,
  output [31:0] AlU_result
);

  wire ALU_PART_e_flag, ALU_PART_gt_flag, and_1_out, and_2_out;
  wire [31:0] multiplexer_1_out;

  Multiplexer #(.width(32), .enable("false")) multiplexer_1 (
    .in0(op2), .in1(immx), .out(multiplexer_1_out), .sel(is_immx));
  and and_1 (and_1_out, isBgt, flag_GT);
  D_Flip_Flop #(.trigger("falling")) GT__flag (
    .clk(clock), .D(ALU_PART_gt_flag), .Q(flag_GT), .en(ALUsignals[0]));  // open: Qn, preset, reset
  alu ALU_PART (
    .A(op1), .B(multiplexer_1_out), .ALUsignals(ALUsignals), .Aluresult(AlU_result),
    .GT_flag(ALU_PART_gt_flag), .E_flag(ALU_PART_e_flag));
  and and_2 (and_2_out, isBeq, flag_E);
  D_Flip_Flop #(.trigger("falling")) E_flag (
    .clk(clock), .D(ALU_PART_e_flag), .Q(flag_E), .en(ALUsignals[0]));  // open: Qn, preset, reset
  or or_1 (Is_Branch_Taken, Is_uBranch, and_1_out, and_2_out);
endmodule
